# Fritzing sketch ESP32-03-Button (saved by Fritzing 0.9.3b)
breadboards: 1

parts:
  A1 = Esp32-c3 super mini
  S1 = Pushbutton [package="[SMD]"]

nets:
  N1: A1.Pin_6, S1.Pin_1, S1.Pin_2
  N2: A1.Pin_15, S1.Pin_3, S1.Pin_4

custom parts:
  Esp32-c3 super mini: ESP32-C3 Development Board ESP32 SuperMini Development Board ESP32 Development Board WiFi Bluetooth.
