# Fritzing sketch ESP32-04-Potmeter (saved by Fritzing 0.9.6b)
breadboards: 1

parts:
  A1 = Esp32-c3 super mini
  U1 = POT [package=pot_alpha_rv16af-20]

nets:
  N1: A1.Pin_12, U1.S
  N2: A1.Pin_14, U1.E
  N3: A1.Pin_15, U1.A

custom parts:
  Esp32-c3 super mini: ESP32-C3 Development Board ESP32 SuperMini Development Board ESP32 Development Board WiFi Bluetooth.
