# Fritzing sketch ESP32-05-PIR (saved by Fritzing 1.0.1rc)
breadboards: 1

parts:
  A1 = Esp32-c3 super mini
  PIR1 = PIR sensor
  L1 = Inductor [package="400 mil [THT]"]

nets:
  N1: A1.Pin_6, L1.pin_1
  N2: A1.Pin_14, PIR1.VDD
  N3: A1.Pin_15, PIR1.GND
  N4: PIR1.SIG, L1.pin_0

notes:
  Inductor is ferrite bead

custom parts:
  Esp32-c3 super mini: ESP32-C3 Development Board ESP32 SuperMini Development Board ESP32 Development Board WiFi Bluetooth.
