# Fritzing sketch ESP32-06-Temp_sensor (saved by Fritzing 1.0.1rc)
breadboards: 1

parts:
  A1 = Esp32-c3 super mini
  DS2 = DS18B20 1-Wire Temperature Sensor [part_number=DS18B20]
  R1 = Resistor [tolerance=±5% resistance=4.7k package="2010 [SMD]"]

nets:
  N1: A1.Pin_6, DS2.DQ, R1.Pin_0
  N2: A1.Pin_14, DS2.VDD, R1.Pin_1
  N3: A1.Pin_15, DS2.GND

custom parts:
  Esp32-c3 super mini: ESP32-C3 Development Board ESP32 SuperMini Development Board ESP32 Development Board WiFi Bluetooth.
