# Fritzing sketch ESP32-06-Temperatursensor (saved by Fritzing 0.9.6b)
breadboards: 1

parts:
  A1 = Esp32-c3 super mini
  DS1 = DS18B20 1-Wire Temperature Sensor Probe
  PIR1 = PIR sensor  # not connected

nets:
  N1: A1.Pin_6, DS1.DQ
  N2: A1.Pin_14, DS1.VDD
  N3: A1.Pin_15, DS1.GND

custom parts:
  Esp32-c3 super mini: ESP32-C3 Development Board ESP32 SuperMini Development Board ESP32 Development Board WiFi Bluetooth.
