# Fritzing sketch ESP32-10-Binary_counter (saved by Fritzing 0.9.3b)
breadboards: 1

parts:
  A1 = Esp32-c3 super mini
  LED1 = smd LED [color="Red (633nm)" package="0603 [SMD]"]
  LED2 = smd LED [color="Red (633nm)" package="0603 [SMD]"]
  LED3 = smd LED [color="Red (633nm)" package="0603 [SMD]"]
  LED4 = smd LED [color="Red (633nm)" package="0603 [SMD]"]

nets:
  N1: A1.Pin_9, LED1.anode
  N2: A1.Pin_10, LED2.anode
  N3: A1.Pin_11, LED3.anode
  N4: A1.Pin_12, LED4.anode
  N5: A1.Pin_15, LED1.cathode, LED2.cathode, LED3.cathode, LED4.cathode

custom parts:
  Esp32-c3 super mini: ESP32-C3 Development Board ESP32 SuperMini Development Board ESP32 Development Board WiFi Bluetooth.
