# Fritzing sketch ESP32-12-Display_counter (saved by Fritzing 0.9.3b)
breadboards: 1

parts:
  A1 = Esp32-c3 super mini
  A2 = Hiletgo 8digit led display

nets (from the breadboard view):
  N1: A1.Pin_2, A2.Pin_5
  N2: A1.Pin_3, A2.Pin_4
  N3: A1.Pin_6, A2.Pin_3
  N4: A1.Pin_15, A2.Pin_2
  N5: A1.Pin_16, A2.Pin_1

custom parts:
  Esp32-c3 super mini: ESP32-C3 Development Board ESP32 SuperMini Development Board ESP32 Development Board WiFi Bluetooth.
  Hiletgo 8digit led display: MAX7219 is an integrated serial input / output common-cathode display driver, which connects your microprocessor to a 7-segment digital LED display with 8 digits.
