# Fritzing sketch ESP32-13-Neopixel_counter (saved by Fritzing 0.9.3b)
breadboards: 1

parts:
  A1 = Esp32-c3 super mini
  U1 = WS2812 RGB LED strip

nets:
  N1: A1.Pin_6, U1.DIN
  N2: A1.Pin_14, U1.VCC
  N3: A1.Pin_15, U1.GND

custom parts:
  Esp32-c3 super mini: ESP32-C3 Development Board ESP32 SuperMini Development Board ESP32 Development Board WiFi Bluetooth.
  WS2812 RGB LED strip: WS2812 strip
