# Fritzing sketch ESP32-15-Potmeter-LED_display (saved by Fritzing 0.9.3b)
breadboards: 1

parts:
  A1 = Esp32-c3 super mini
  A2 = Hiletgo 8digit led display
  U3 = POT [package=pot_alpha_rv16af-20]

nets:
  N1: A1.Pin_2, A2.Pin_5
  N2: A1.Pin_3, A2.Pin_4
  N3: A1.Pin_6, A2.Pin_3
  N4: A1.Pin_9, U3.S
  N5: A1.Pin_14, A2.Pin_1, A2.Pin_10, U3.A
  N6: A1.Pin_15, A2.Pin_2, A2.Pin_9, U3.E

custom parts:
  Esp32-c3 super mini: ESP32-C3 Development Board ESP32 SuperMini Development Board ESP32 Development Board WiFi Bluetooth.
  Hiletgo 8digit led display: MAX7219 is an integrated serial input / output common-cathode display driver, which connects your microprocessor to a 7-segment digital LED display with 8 digits.
