# Fritzing sketch ESP32-16-Tempsensor-Display (saved by Fritzing 0.9.3b)
breadboards: 1

parts:
  A1 = Esp32-c3 super mini
  A2 = Hiletgo 8digit led display
  DS3 = DS18B20 1-Wire Temperature Sensor [part_number=DS18B20]
  R1 = Resistor [tolerance=±5% resistance=4.7k package="2010 [SMD]"]

nets (from the breadboard view):
  N1: A1.Pin_1, A2.Pin_5, A2.Pin_6
  N2: A1.Pin_2, A2.Pin_4
  N3: A1.Pin_3, A2.Pin_3
  N4: A1.Pin_6, DS3.DQ, R1.Pin_0
  N5: A1.Pin_14, A2.Pin_1, A2.Pin_10, DS3.VDD, R1.Pin_1
  N6: A1.Pin_15, A2.Pin_2, A2.Pin_9, DS3.GND

custom parts:
  Esp32-c3 super mini: ESP32-C3 Development Board ESP32 SuperMini Development Board ESP32 Development Board WiFi Bluetooth.
  Hiletgo 8digit led display: MAX7219 is an integrated serial input / output common-cathode display driver, which connects your microprocessor to a 7-segment digital LED display with 8 digits.
